// Logisim project project1.circ as structural Verilog: 5 circuits, main circuit main
module main (
);

  wire bto7_seg_1_a, bto7_seg_1_b, bto7_seg_1_c, bto7_seg_1_d, bto7_seg_1_e, bto7_seg_1_f, bto7_seg_1_g,
       bto7_seg_2_a, bto7_seg_2_b, bto7_seg_2_c, bto7_seg_2_d, bto7_seg_2_e, bto7_seg_2_f, bto7_seg_2_g,
       bto7_seg_3_a, bto7_seg_3_b, bto7_seg_3_c, bto7_seg_3_d, bto7_seg_3_e, bto7_seg_3_f, bto7_seg_3_g,
       bto7_seg_4_a, bto7_seg_4_b, bto7_seg_4_c, bto7_seg_4_d, bto7_seg_4_e, bto7_seg_4_f, bto7_seg_4_g,
       bto7_seg_5_a, bto7_seg_5_b, bto7_seg_5_c, bto7_seg_5_d, bto7_seg_5_e, bto7_seg_5_f, bto7_seg_5_g,
       bto7_seg_6_a, bto7_seg_6_b, bto7_seg_6_c, bto7_seg_6_d, bto7_seg_6_e, bto7_seg_6_f, bto7_seg_6_g,
       hrs_1_hrs_input, sec_count_1_min_input;
  wire [4:0] final_1_hrs, final_1_hrs_10, hrs_1_min, hrs_1_ten_min, sec_count_1_sec, sec_count_1_ten_sec;

  Bto7_seg bto7_seg_1 (
    .five_bit_in(final_1_hrs_10), .a(bto7_seg_1_a), .b(bto7_seg_1_b), .c(bto7_seg_1_c), .d(bto7_seg_1_d),
    .e(bto7_seg_1_e), .f(bto7_seg_1_f), .g(bto7_seg_1_g));  // open: CarryOut
  _7_Segment_Display u_7_segment_display_1 (
    .g(bto7_seg_1_g), .f(bto7_seg_1_f), .a(bto7_seg_1_a), .b(bto7_seg_1_b), .e(bto7_seg_1_e),
    .d(bto7_seg_1_d), .c(bto7_seg_1_c));  // open: dp
  \final  final_1 (.final_in(hrs_1_hrs_input), .hrs_10(final_1_hrs_10), .hrs(final_1_hrs));
  Bto7_seg bto7_seg_2 (
    .five_bit_in(final_1_hrs), .a(bto7_seg_2_a), .b(bto7_seg_2_b), .c(bto7_seg_2_c), .d(bto7_seg_2_d),
    .e(bto7_seg_2_e), .f(bto7_seg_2_f), .g(bto7_seg_2_g));  // open: CarryOut
  _7_Segment_Display u_7_segment_display_2 (
    .g(bto7_seg_2_g), .f(bto7_seg_2_f), .a(bto7_seg_2_a), .b(bto7_seg_2_b), .e(bto7_seg_2_e),
    .d(bto7_seg_2_d), .c(bto7_seg_2_c));  // open: dp
  Bto7_seg bto7_seg_3 (
    .five_bit_in(hrs_1_ten_min), .a(bto7_seg_3_a), .b(bto7_seg_3_b), .c(bto7_seg_3_c), .d(bto7_seg_3_d),
    .e(bto7_seg_3_e), .f(bto7_seg_3_f), .g(bto7_seg_3_g));  // open: CarryOut
  _7_Segment_Display u_7_segment_display_3 (
    .g(bto7_seg_3_g), .f(bto7_seg_3_f), .a(bto7_seg_3_a), .b(bto7_seg_3_b), .e(bto7_seg_3_e),
    .d(bto7_seg_3_d), .c(bto7_seg_3_c));  // open: dp
  hrs hrs_1 (.hrs_input(hrs_1_hrs_input), .min_input(sec_count_1_min_input), .ten_min(hrs_1_ten_min), .min(hrs_1_min));
  Bto7_seg bto7_seg_4 (
    .five_bit_in(hrs_1_min), .a(bto7_seg_4_a), .b(bto7_seg_4_b), .c(bto7_seg_4_c), .d(bto7_seg_4_d),
    .e(bto7_seg_4_e), .f(bto7_seg_4_f), .g(bto7_seg_4_g));  // open: CarryOut
  _7_Segment_Display u_7_segment_display_4 (
    .g(bto7_seg_4_g), .f(bto7_seg_4_f), .a(bto7_seg_4_a), .b(bto7_seg_4_b), .e(bto7_seg_4_e),
    .d(bto7_seg_4_d), .c(bto7_seg_4_c));  // open: dp
  Bto7_seg bto7_seg_5 (
    .five_bit_in(sec_count_1_ten_sec), .a(bto7_seg_5_a), .b(bto7_seg_5_b), .c(bto7_seg_5_c),
    .d(bto7_seg_5_d), .e(bto7_seg_5_e), .f(bto7_seg_5_f), .g(bto7_seg_5_g));  // open: CarryOut
  _7_Segment_Display u_7_segment_display_5 (
    .g(bto7_seg_5_g), .f(bto7_seg_5_f), .a(bto7_seg_5_a), .b(bto7_seg_5_b), .e(bto7_seg_5_e),
    .d(bto7_seg_5_d), .c(bto7_seg_5_c));  // open: dp
  sec_count sec_count_1 (.min_input(sec_count_1_min_input), .ten_sec(sec_count_1_ten_sec), .sec(sec_count_1_sec));
  Bto7_seg bto7_seg_6 (
    .five_bit_in(sec_count_1_sec), .a(bto7_seg_6_a), .b(bto7_seg_6_b), .c(bto7_seg_6_c), .d(bto7_seg_6_d),
    .e(bto7_seg_6_e), .f(bto7_seg_6_f), .g(bto7_seg_6_g));  // open: CarryOut
  _7_Segment_Display u_7_segment_display_6 (
    .g(bto7_seg_6_g), .f(bto7_seg_6_f), .a(bto7_seg_6_a), .b(bto7_seg_6_b), .e(bto7_seg_6_e),
    .d(bto7_seg_6_d), .c(bto7_seg_6_c));  // open: dp

  // Notes on the sheet:
  //   hours counter
  //   Hours
  //   24 Hours Clock
  //   Minutes
  //   minutes counter
  //   Seconds
  //   seconds counter
endmodule

module Bto7_seg (
  input  [4:0] five_bit_in,
  output a,
  output b,
  output c,
  output d,
  output e,
  output f,
  output g,
  output CarryOut
);

  wire and_1_out, and_2_out, and_3_out, and_4_out, and_5_out, and_6_out, and_7_out, and_8_out, and_9_out,
       and_10_out, and_11_out, and_12_out, and_13_out, and_14_out, and_15_out, and_16_out, and_17_out,
       and_18_out, and_19_out, and_20_out, and_21_out, and_22_out, and_23_out, and_24_out, and_25_out,
       and_26_out, and_27_out, and_28_out, and_29_out, and_30_out, and_31_out, and_32_out, and_33_out,
       and_34_out, and_35_out, and_36_out, and_37_out, and_38_out, and_39_out, and_40_out, and_41_out,
       and_42_out, and_43_out, and_44_out, and_45_out, and_46_out, and_47_out, and_48_out, and_49_out,
       and_50_out, and_51_out, and_52_out, and_53_out, and_54_out, and_55_out, and_56_out, and_57_out,
       and_58_out, and_59_out, and_60_out, not_1_out, not_2_out, not_3_out, not_4_out, not_5_out, not_6_out,
       not_7_out, not_8_out, not_9_out, not_10_out, not_11_out, not_12_out, not_13_out, not_14_out,
       not_15_out, not_16_out, not_17_out, not_18_out, not_19_out, not_20_out, not_21_out, not_22_out,
       not_23_out, not_24_out, not_25_out, not_26_out, not_27_out, not_28_out, not_29_out, not_30_out,
       not_31_out, not_32_out, not_33_out, not_34_out, not_35_out, not_36_out, not_37_out, not_38_out,
       not_39_out, not_40_out, not_41_out, not_42_out, not_43_out, not_44_out, not_45_out, not_46_out,
       not_47_out, not_48_out, not_49_out, not_50_out, not_51_out, not_52_out, not_53_out, not_54_out,
       not_55_out, not_56_out, not_57_out, not_58_out, not_59_out, not_60_out, not_61_out, not_62_out,
       not_63_out, not_64_out, not_65_out, not_66_out, not_67_out, not_68_out, not_69_out, not_70_out,
       not_71_out, not_72_out, not_73_out, not_74_out, not_75_out, not_76_out, not_77_out, not_78_out,
       not_79_out, not_80_out, not_81_out, not_82_out, not_83_out, not_84_out, not_85_out, not_86_out,
       not_87_out, not_88_out, not_89_out, not_90_out, not_91_out, not_92_out, not_93_out, not_94_out,
       not_95_out, not_96_out, not_97_out, not_98_out, not_99_out, not_100_out, not_101_out, not_102_out,
       not_103_out, not_104_out, not_105_out, not_106_out, not_107_out, not_108_out, not_109_out;

  not not_1 (not_1_out, five_bit_in[4]);
  not not_2 (not_2_out, five_bit_in[2]);
  not not_3 (not_3_out, five_bit_in[0]);
  not not_4 (not_4_out, five_bit_in[3]);
  not not_5 (not_5_out, five_bit_in[4]);
  not not_6 (not_6_out, five_bit_in[4]);
  not not_7 (not_7_out, five_bit_in[1]);
  not not_8 (not_8_out, five_bit_in[1]);
  not not_9 (not_9_out, five_bit_in[3]);
  not not_10 (not_10_out, five_bit_in[0]);
  not not_11 (not_11_out, five_bit_in[2]);
  not not_12 (not_12_out, five_bit_in[0]);
  not not_13 (not_13_out, five_bit_in[4]);
  not not_14 (not_14_out, five_bit_in[2]);
  not not_15 (not_15_out, five_bit_in[4]);
  not not_16 (not_16_out, five_bit_in[1]);
  not not_17 (not_17_out, five_bit_in[0]);
  not not_18 (not_18_out, five_bit_in[3]);
  not not_19 (not_19_out, five_bit_in[2]);
  not not_20 (not_20_out, five_bit_in[3]);
  not not_21 (not_21_out, five_bit_in[2]);
  not not_22 (not_22_out, five_bit_in[3]);
  not not_23 (not_23_out, five_bit_in[2]);
  not not_24 (not_24_out, five_bit_in[4]);
  not not_25 (not_25_out, five_bit_in[0]);
  not not_26 (not_26_out, five_bit_in[1]);
  not not_27 (not_27_out, five_bit_in[0]);
  not not_28 (not_28_out, five_bit_in[1]);
  not not_29 (not_29_out, five_bit_in[3]);
  not not_30 (not_30_out, five_bit_in[1]);
  not not_31 (not_31_out, five_bit_in[4]);
  not not_32 (not_32_out, five_bit_in[3]);
  not not_33 (not_33_out, five_bit_in[2]);
  not not_34 (not_34_out, five_bit_in[2]);
  not not_35 (not_35_out, five_bit_in[1]);
  not not_36 (not_36_out, five_bit_in[4]);
  not not_37 (not_37_out, five_bit_in[2]);
  not not_38 (not_38_out, five_bit_in[0]);
  not not_39 (not_39_out, five_bit_in[3]);
  not not_40 (not_40_out, five_bit_in[2]);
  not not_41 (not_41_out, five_bit_in[0]);
  not not_42 (not_42_out, five_bit_in[3]);
  not not_43 (not_43_out, five_bit_in[2]);
  not not_44 (not_44_out, five_bit_in[3]);
  not not_45 (not_45_out, five_bit_in[0]);
  not not_46 (not_46_out, five_bit_in[2]);
  not not_47 (not_47_out, five_bit_in[0]);
  not not_48 (not_48_out, five_bit_in[4]);
  not not_49 (not_49_out, five_bit_in[1]);
  not not_50 (not_50_out, five_bit_in[1]);
  not not_51 (not_51_out, five_bit_in[1]);
  not not_52 (not_52_out, five_bit_in[4]);
  not not_53 (not_53_out, five_bit_in[3]);
  not not_54 (not_54_out, five_bit_in[0]);
  not not_55 (not_55_out, five_bit_in[4]);
  not not_56 (not_56_out, five_bit_in[2]);
  not not_57 (not_57_out, five_bit_in[0]);
  not not_58 (not_58_out, five_bit_in[3]);
  not not_59 (not_59_out, five_bit_in[2]);
  not not_60 (not_60_out, five_bit_in[0]);
  not not_61 (not_61_out, five_bit_in[3]);
  not not_62 (not_62_out, five_bit_in[0]);
  not not_63 (not_63_out, five_bit_in[2]);
  not not_64 (not_64_out, five_bit_in[0]);
  not not_65 (not_65_out, five_bit_in[4]);
  not not_66 (not_66_out, five_bit_in[1]);
  not not_67 (not_67_out, five_bit_in[0]);
  not not_68 (not_68_out, five_bit_in[0]);
  not not_69 (not_69_out, five_bit_in[3]);
  not not_70 (not_70_out, five_bit_in[1]);
  not not_71 (not_71_out, five_bit_in[0]);
  not not_72 (not_72_out, five_bit_in[4]);
  not not_73 (not_73_out, five_bit_in[3]);
  not not_74 (not_74_out, five_bit_in[1]);
  not not_75 (not_75_out, five_bit_in[4]);
  not not_76 (not_76_out, five_bit_in[3]);
  not not_77 (not_77_out, five_bit_in[0]);
  not not_78 (not_78_out, five_bit_in[2]);
  not not_79 (not_79_out, five_bit_in[1]);
  not not_80 (not_80_out, five_bit_in[0]);
  not not_81 (not_81_out, five_bit_in[4]);
  not not_82 (not_82_out, five_bit_in[3]);
  not not_83 (not_83_out, five_bit_in[2]);
  not not_84 (not_84_out, five_bit_in[1]);
  not not_85 (not_85_out, five_bit_in[3]);
  not not_86 (not_86_out, five_bit_in[2]);
  not not_87 (not_87_out, five_bit_in[3]);
  not not_88 (not_88_out, five_bit_in[0]);
  not not_89 (not_89_out, five_bit_in[4]);
  not not_90 (not_90_out, five_bit_in[1]);
  not not_91 (not_91_out, five_bit_in[1]);
  not not_92 (not_92_out, five_bit_in[4]);
  not not_93 (not_93_out, five_bit_in[2]);
  not not_94 (not_94_out, five_bit_in[0]);
  not not_95 (not_95_out, five_bit_in[3]);
  not not_96 (not_96_out, five_bit_in[4]);
  not not_97 (not_97_out, five_bit_in[2]);
  not not_98 (not_98_out, five_bit_in[0]);
  not not_99 (not_99_out, five_bit_in[3]);
  not not_100 (not_100_out, five_bit_in[1]);
  not not_101 (not_101_out, five_bit_in[0]);
  not not_102 (not_102_out, five_bit_in[2]);
  not not_103 (not_103_out, five_bit_in[1]);
  not not_104 (not_104_out, five_bit_in[0]);
  not not_105 (not_105_out, five_bit_in[4]);
  not not_106 (not_106_out, five_bit_in[3]);
  not not_107 (not_107_out, five_bit_in[2]);
  not not_108 (not_108_out, five_bit_in[1]);
  not not_109 (not_109_out, five_bit_in[0]);
  and and_1 (and_1_out, not_1_out, not_2_out, not_3_out);
  and and_2 (and_2_out, not_4_out, five_bit_in[1]);
  and and_3 (and_3_out, not_5_out, five_bit_in[2], five_bit_in[0]);
  and and_4 (and_4_out, not_6_out, five_bit_in[3], not_7_out);
  and and_5 (and_5_out, five_bit_in[3], five_bit_in[2], not_8_out);
  and and_6 (and_6_out, five_bit_in[4], not_9_out, not_10_out);
  and and_7 (and_7_out, five_bit_in[4], not_11_out, five_bit_in[0]);
  and and_8 (and_8_out, five_bit_in[4], five_bit_in[1], not_12_out);
  and and_9 (and_9_out, not_13_out, not_14_out);
  and and_10 (and_10_out, not_15_out, not_16_out, not_17_out);
  and and_11 (and_11_out, not_18_out, not_19_out, five_bit_in[0]);
  and and_12 (and_12_out, not_20_out, not_21_out, five_bit_in[1]);
  and and_13 (and_13_out, not_22_out, five_bit_in[1], five_bit_in[0]);
  and and_14 (and_14_out, not_23_out, five_bit_in[1], five_bit_in[0]);
  and and_15 (and_15_out, not_24_out, five_bit_in[3], not_25_out);
  and and_16 (and_16_out, five_bit_in[3], not_26_out, not_27_out);
  and and_17 (and_17_out, five_bit_in[3], five_bit_in[2], not_28_out);
  and and_18 (and_18_out, five_bit_in[4], five_bit_in[2]);
  and and_19 (and_19_out, not_29_out, not_30_out);
  and and_20 (and_20_out, not_31_out, not_32_out, five_bit_in[2]);
  and and_21 (and_21_out, five_bit_in[3], not_33_out);
  and and_22 (and_22_out, five_bit_in[3], five_bit_in[1]);
  and and_23 (and_23_out, five_bit_in[4], not_34_out);
  and and_24 (and_24_out, five_bit_in[4], not_35_out);
  and and_25 (and_25_out, not_36_out, not_37_out, not_38_out);
  and and_26 (and_26_out, not_39_out, not_40_out, not_41_out);
  and and_27 (and_27_out, not_42_out, not_43_out, five_bit_in[1]);
  and and_28 (and_28_out, not_44_out, five_bit_in[1], not_45_out);
  and and_29 (and_29_out, not_46_out, five_bit_in[1], not_47_out);
  and and_30 (and_30_out, not_48_out, five_bit_in[2], not_49_out, five_bit_in[0]);
  and and_31 (and_31_out, five_bit_in[3], not_50_out, five_bit_in[0]);
  and and_32 (and_32_out, five_bit_in[3], five_bit_in[2], not_51_out);
  and and_33 (and_33_out, not_52_out, five_bit_in[3], five_bit_in[2], five_bit_in[0]);
  and and_34 (and_34_out, five_bit_in[4], not_53_out, five_bit_in[1]);
  and and_35 (and_35_out, five_bit_in[4], five_bit_in[2], not_54_out);
  and and_36 (and_36_out, not_55_out, not_56_out, not_57_out);
  and and_37 (and_37_out, not_58_out, not_59_out, not_60_out);
  and and_38 (and_38_out, not_61_out, five_bit_in[1], not_62_out);
  and and_39 (and_39_out, not_63_out, five_bit_in[1], not_64_out);
  and and_40 (and_40_out, not_65_out, five_bit_in[3], not_66_out, not_67_out);
  and and_41 (and_41_out, five_bit_in[4], five_bit_in[2], not_68_out);
  and and_42 (and_42_out, not_69_out, not_70_out, not_71_out);
  and and_43 (and_43_out, not_72_out, not_73_out, five_bit_in[2], not_74_out);
  and and_44 (and_44_out, not_75_out, not_76_out, five_bit_in[2], not_77_out);
  and and_45 (and_45_out, five_bit_in[3], not_78_out, not_79_out);
  and and_46 (and_46_out, five_bit_in[3], five_bit_in[1], not_80_out);
  and and_47 (and_47_out, not_81_out, five_bit_in[3], five_bit_in[2], five_bit_in[1]);
  and and_48 (and_48_out, five_bit_in[4], not_82_out, not_83_out, five_bit_in[1]);
  and and_49 (and_49_out, five_bit_in[4], five_bit_in[3], not_84_out);
  and and_50 (and_50_out, not_85_out, not_86_out, five_bit_in[1]);
  and and_51 (and_51_out, not_87_out, five_bit_in[1], not_88_out);
  and and_52 (and_52_out, not_89_out, five_bit_in[2], not_90_out);
  and and_53 (and_53_out, five_bit_in[3], not_91_out);
  and and_54 (and_54_out, not_92_out, five_bit_in[3], five_bit_in[2]);
  and and_55 (and_55_out, five_bit_in[4], not_93_out, not_94_out);
  and and_56 (and_56_out, five_bit_in[4], not_95_out, five_bit_in[1]);
  and and_57 (and_57_out, five_bit_in[3], five_bit_in[1]);
  and and_58 (and_58_out, not_99_out, not_100_out);
  and and_59 (and_59_out, five_bit_in[3], not_103_out);
  and and_60 (and_60_out, not_106_out, not_108_out);
  or or_1 (a, and_1_out, and_2_out, and_3_out, and_4_out, and_5_out, and_6_out, and_7_out, and_8_out);
  or or_2 (b, and_9_out, and_10_out, and_11_out, and_12_out, and_13_out, and_14_out, and_15_out, and_16_out, and_17_out, and_18_out);
  or or_3 (c, and_19_out, five_bit_in[0], and_20_out, and_21_out, and_22_out, and_23_out, and_24_out);
  or or_4 (d, and_25_out, and_26_out, and_27_out, and_28_out, and_29_out, and_30_out, and_31_out, and_32_out, and_33_out, and_34_out, and_35_out);
  or or_5 (e, and_36_out, and_37_out, and_38_out, and_39_out, and_40_out, and_41_out);
  or or_6 (f, and_42_out, and_43_out, and_44_out, and_45_out, and_46_out, and_47_out, and_48_out, and_49_out);
  or or_7 (g, and_50_out, and_51_out, and_52_out, and_53_out, and_54_out, and_55_out, and_56_out);
  or or_8 (CarryOut, and_57_out, and_58_out, and_59_out, and_60_out);
endmodule

module sec_count (
  output min_input,
  output [4:0] ten_sec,
  output [4:0] sec
);

  wire decoder_2_out10, input_out;

  Clock sysclk ();  // open: out
  Counter #(.width(5), .max('h6)) counter_1 (
    .clr(min_input), .clk(decoder_2_out10), .Q(ten_sec));  // open: load, up, count, D, carry
  Decoder #(.select(5)) decoder_1 (
    .out6(min_input), .sel(ten_sec));  // open: out0, out1, out2, out3, out4, out5, out7, out8, out9, out10, out11, out12, out13, out14, out15, out16, out17, out18, out19, out20, out21, out22, out23, out24, out25, out26, out27, out28, out29, out30, out31, en
  Clock \input  (.out(input_out));
  Counter #(.width(5), .max('h10)) counter_2 (
    .clr(decoder_2_out10), .clk(input_out), .Q(sec));  // open: load, up, count, D, carry
  Decoder #(.select(5)) decoder_2 (
    .out10(decoder_2_out10), .sel(sec));  // open: out0, out1, out2, out3, out4, out5, out6, out7, out8, out9, out11, out12, out13, out14, out15, out16, out17, out18, out19, out20, out21, out22, out23, out24, out25, out26, out27, out28, out29, out30, out31, en
endmodule

module hrs (
  input  min_input,
  output hrs_input,
  output [4:0] ten_min,
  output [4:0] min
);

  wire decoder_2_out10;

  Counter #(.width(5), .max('h6)) counter_1 (
    .clr(hrs_input), .clk(decoder_2_out10), .Q(ten_min));  // open: load, up, count, D, carry
  Decoder #(.select(5)) decoder_1 (
    .out6(hrs_input), .sel(ten_min));  // open: out0, out1, out2, out3, out4, out5, out7, out8, out9, out10, out11, out12, out13, out14, out15, out16, out17, out18, out19, out20, out21, out22, out23, out24, out25, out26, out27, out28, out29, out30, out31, en
  Counter #(.width(5), .max('h10)) counter_2 (
    .clr(decoder_2_out10), .clk(min_input), .Q(min));  // open: load, up, count, D, carry
  Decoder #(.select(5)) decoder_2 (
    .out10(decoder_2_out10), .sel(min));  // open: out0, out1, out2, out3, out4, out5, out6, out7, out8, out9, out11, out12, out13, out14, out15, out16, out17, out18, out19, out20, out21, out22, out23, out24, out25, out26, out27, out28, out29, out30, out31, en
endmodule

module \final  (
  input  final_in,
  output [4:0] hrs_10,
  output [4:0] hrs
);

  wire and_1_out, decoder_1_out2, decoder_2_out4, decoder_2_out10, or_1_out;

  Counter #(.width(5), .max('h5)) counter_1 (
    .clr(and_1_out), .clk(decoder_2_out10), .Q(hrs_10));  // open: load, up, count, D, carry
  Decoder #(.select(5)) decoder_1 (
    .out2(decoder_1_out2), .sel(hrs_10));  // open: out0, out1, out3, out4, out5, out6, out7, out8, out9, out10, out11, out12, out13, out14, out15, out16, out17, out18, out19, out20, out21, out22, out23, out24, out25, out26, out27, out28, out29, out30, out31, en
  and and_1 (and_1_out, decoder_1_out2, decoder_2_out4);
  Counter #(.width(5), .max('h10)) counter_2 (
    .clr(or_1_out), .clk(final_in), .Q(hrs));  // open: load, up, count, D, carry
  or or_1 (or_1_out, and_1_out, decoder_2_out10);
  Decoder #(.select(5)) decoder_2 (
    .out4(decoder_2_out4), .out10(decoder_2_out10), .sel(hrs));  // open: out0, out1, out2, out3, out5, out6, out7, out8, out9, out11, out12, out13, out14, out15, out16, out17, out18, out19, out20, out21, out22, out23, out24, out25, out26, out27, out28, out29, out30, out31, en
endmodule
